# Fritzing sketch TwoButtonLEDBrightness (saved by Fritzing 0.9.2b)
breadboards: 1

parts:
  R1 = Resistor [tolerance=±5% resistance=220 package=THT]
  S1 = Pushbutton [package="[THT]"]
  S2 = Pushbutton [package="[THT]"]
  LED1 = LED - 5mm [color="Red (633nm)" package="5 mm [THT]"]
  Part1 = Arduino Uno (Rev3) - ICSP
  R2 = Resistor [tolerance=±5% resistance=10k package="1206 [SMD]"]
  R3 = Resistor [tolerance=±5% resistance=10k package="1206 [SMD]"]

nets:
  N1: R1.Pin_0, LED1.anode
  N2: R1.Pin_1, Part1.ICSP_MOSI, Part1.D11_PWM/MOSI
  N3: S1.Pin_1, S1.Pin_2, Part1.D3_PWM, R2.Pin_0
  N4: S1.Pin_3, S1.Pin_4, S2.Pin_3, S2.Pin_4, Part1.5V
  N5: S2.Pin_1, S2.Pin_2, Part1.D2, R3.Pin_0
  N6: LED1.cathode, Part1.GND, R2.Pin_1, R3.Pin_1

// code stored in the sketch: TwobButtonLEDBrightness.ino
var five = require("johnny-five"),
board, button;

board = new five.Board();

board.on("ready", function() {

  // Create a new `button` hardware instance.
  // This example allows the button module to
  // create a completely default instance
  button1 = new five.Button({
    board: board,
    pin: 2,
    holdtime: 500,
    invert: false // Default: "false".  Set to "true" if button is Active-Low
  });
  button2 = new five.Button({
    board: board,
    pin: 3,
    holdtime: 500,
    invert: false // Default: "false".  Set to "true" if button is Active-Low
  });

  var led = new five.Led(11);
  var brightness = 0; //start brightness
  
  // Inject the `button` hardware into
  // the Repl instance's context;
  // allows direct command line access
  board.repl.inject({
    button1: button1, 
	button2: button2, 
  });

  // Button Event API

  // "hold" the button is pressed for specified time.
  //        defaults to 500ms (1/2 second)
  //        set
  button1.on("hold", function() {
	  brightness = brightness+10
	  if (brightness>255) brightness = 255;
	  led.brightness(brightness); 
	  console.log(brightness);	
  });
  button2.on("hold", function() {
	  brightness = brightness-10
	  if (brightness<0) brightness = 0;
	  led.brightness(brightness); 
	  console.log(brightness);	
  });

  /*
  // "down" the button is pressed
  button1.on("down", function() {
    console.log("down");
  });
  
  // "up" the button is released
  button1.on("up", function() {
    console.log("up");
  });
  */
});
